// Logisim project Project.circ as structural Verilog
module Half_Adder (
  input  in_1,
  input  in_2,
  output out_3,
  output out_4
);

  wire not_1_out, or_1_out;

  or or_1 (or_1_out, in_1, in_2);
  and and_1 (out_4, in_1, in_2);
  and and_2 (out_3, or_1_out, not_1_out);
  not not_1 (not_1_out, out_4);
endmodule

module Full_Adder (
  input  in_1,
  input  in_2,
  input  in_3,
  output out_4,
  output out_5
);

  wire half_adder_1_out_3, half_adder_1_out_4, half_adder_2_out_4;

  Half_Adder half_adder_1 (.in_1(in_1), .in_2(in_2), .out_3(half_adder_1_out_3), .out_4(half_adder_1_out_4));
  Half_Adder half_adder_2 (.in_1(half_adder_1_out_3), .in_2(in_3), .out_3(out_4), .out_4(half_adder_2_out_4));
  or or_1 (out_5, half_adder_2_out_4, half_adder_1_out_4);
endmodule

module Addition (
  input  [7:0] ALU_Left,
  input  [7:0] ALU_Right,
  output [7:0] ALU_Out,
  output [3:0] out_4
);

  wire full_adder_1_out_5, full_adder_2_out_5, full_adder_3_out_5, full_adder_4_out_5, full_adder_5_out_5,
       full_adder_6_out_5, half_adder_1_out_4, not_1_out, not_2_out, not_3_out, not_4_out, not_5_out,
       not_6_out, not_7_out, not_8_out;

  Half_Adder half_adder_1 (.in_1(ALU_Left[0]), .in_2(ALU_Right[0]), .out_3(ALU_Out[0]), .out_4(half_adder_1_out_4));
  Full_Adder full_adder_1 (
    .in_1(half_adder_1_out_4), .in_2(ALU_Right[1]), .in_3(ALU_Left[1]), .out_4(ALU_Out[1]),
    .out_5(full_adder_1_out_5));
  Full_Adder full_adder_2 (
    .in_1(full_adder_1_out_5), .in_2(ALU_Right[2]), .in_3(ALU_Left[2]), .out_4(ALU_Out[2]),
    .out_5(full_adder_2_out_5));
  Full_Adder full_adder_3 (
    .in_1(full_adder_2_out_5), .in_2(ALU_Right[3]), .in_3(ALU_Left[3]), .out_4(ALU_Out[3]),
    .out_5(full_adder_3_out_5));
  Full_Adder full_adder_4 (
    .in_1(full_adder_3_out_5), .in_2(ALU_Right[4]), .in_3(ALU_Left[4]), .out_4(ALU_Out[4]),
    .out_5(full_adder_4_out_5));
  Full_Adder full_adder_5 (
    .in_1(full_adder_4_out_5), .in_2(ALU_Right[5]), .in_3(ALU_Left[5]), .out_4(ALU_Out[5]),
    .out_5(full_adder_5_out_5));
  Full_Adder full_adder_6 (
    .in_1(full_adder_5_out_5), .in_2(ALU_Right[6]), .in_3(ALU_Left[6]), .out_4(ALU_Out[6]),
    .out_5(full_adder_6_out_5));
  Full_Adder full_adder_7 (
    .in_1(full_adder_6_out_5), .in_2(ALU_Right[7]), .in_3(ALU_Left[7]), .out_4(ALU_Out[7]), .out_5(out_4[1]));
  not not_1 (not_1_out, ALU_Out[7]);
  not not_2 (not_2_out, ALU_Out[6]);
  not not_3 (not_3_out, ALU_Out[3]);
  not not_4 (not_4_out, ALU_Out[1]);
  not not_5 (not_5_out, ALU_Out[2]);
  not not_6 (not_6_out, ALU_Out[4]);
  not not_7 (not_7_out, ALU_Out[0]);
  not not_8 (not_8_out, ALU_Out[5]);
  and and_1 (out_4[0], not_1_out, not_2_out, not_8_out, not_6_out, not_3_out, not_5_out, not_4_out, not_7_out);

  assign out_4[3:2] = 2'b00;

  // Notes on the sheet:
  //   Bit 1 - Carry?
  //   Status
  //   Bit 0 - Zero?
endmodule

module _2_s_Complement (
  input  in_1,
  input  in_2,
  input  in_3,
  input  in_4,
  input  in_5,
  input  in_6,
  input  in_7,
  input  in_8,
  output out_9,
  output out_10,
  output out_11,
  output out_12,
  output out_13,
  output out_14,
  output out_15,
  output out_16
);

  wire half_adder_1_out_4, half_adder_2_out_4, half_adder_3_out_4, half_adder_4_out_4, half_adder_5_out_4,
       half_adder_6_out_4, half_adder_7_out_4, not_1_out, not_2_out, not_3_out, not_4_out, not_5_out,
       not_6_out, not_7_out, not_8_out, not_9_out, or_1_out;

  not not_1 (not_1_out, in_2);
  not not_2 (not_2_out, in_1);
  not not_3 (not_3_out, in_6);
  not not_4 (not_4_out, in_3);
  not not_5 (not_5_out, in_4);
  not not_6 (not_6_out, in_5);
  not not_7 (not_7_out, not_8_out);
  not not_8 (not_8_out, in_8);
  not not_9 (not_9_out, in_7);
  or or_1 (or_1_out, not_7_out, not_8_out);
  Half_Adder half_adder_1 (.in_1(or_1_out), .in_2(not_8_out), .out_3(out_16), .out_4(half_adder_1_out_4));
  Half_Adder half_adder_2 (.in_1(half_adder_1_out_4), .in_2(not_9_out), .out_3(out_15), .out_4(half_adder_2_out_4));
  Half_Adder half_adder_3 (.in_1(half_adder_2_out_4), .in_2(not_3_out), .out_3(out_14), .out_4(half_adder_3_out_4));
  Half_Adder half_adder_4 (.in_1(half_adder_3_out_4), .in_2(not_6_out), .out_3(out_13), .out_4(half_adder_4_out_4));
  Half_Adder half_adder_5 (.in_1(half_adder_4_out_4), .in_2(not_5_out), .out_3(out_12), .out_4(half_adder_5_out_4));
  Half_Adder half_adder_6 (.in_1(half_adder_5_out_4), .in_2(not_4_out), .out_3(out_11), .out_4(half_adder_6_out_4));
  Half_Adder half_adder_7 (.in_1(half_adder_6_out_4), .in_2(not_1_out), .out_3(out_10), .out_4(half_adder_7_out_4));
  Half_Adder half_adder_8 (.in_1(half_adder_7_out_4), .in_2(not_2_out), .out_3(out_9));  // open: out_4
endmodule

module ALU (
);

  Addition addition_1 ();  // open: ALU_Out, out_4, ALU_Left, ALU_Right
  _2_s_Complement u_2_s_complement_1 ();  // open: in_1, in_2, in_3, in_4, in_5, in_6, in_7, in_8, out_9, out_10, out_11, out_12, out_13, out_14, out_15, out_16
endmodule
